# Fritzing sketch Harv2 (saved by Fritzing 0.9.3b)
breadboards: 1

parts:
  Part1 = Arduino Uno (Rev3)
  J1 = Basic Servo
  M1 = DC Motor
  M2 = DC Motor
  Q1 = npn-Powertransistor [package="TO220 [THT]"]
  Q2 = npn-Powertransistor [package="TO220 [THT]"]
  D1 = Rectifier Diode [part_number=1N4001 package="300 mil [THT]"]
  D2 = Rectifier Diode [part_number=1N4001 package="300 mil [THT]"]
  Part2 = SRF05 Ultrasonic Rangefinder [part_number="Ultrasonic Sensor HC-SR04"]
  VCC1 = 4 x AAA Battery Mount
  LED1 = smd LED [color="Red (633nm)" package="0805 [SMD]"]  # not connected

nets:
  N1: Part1.D8, Part2.Trig
  N2: Part1.D11_PWM/MOSI, J1.pulse
  N3: Part1.D5_PWM, Q2.emitter
  N4: Part1.D6_PWM, Q1.emitter
  N5: Part1.D7, Part2.Echo
  VCC: Part1.5V, J1.vcc, Part2.VCC
  GND: J1.gnd, Q1.base, Q2.base, Part2.GND, VCC1.-
  N6: M1.pin_1, Q1.collector, D2.anode
  N7: M1.pin_2, M2.pin_1, D1.cathode, D2.cathode, VCC1.+
  N8: M2.pin_2, Q2.collector, D1.anode
